// Logisim project SamoseykoKostinNoughtsCrosses.circ as structural Verilog: 5 circuits, main circuit Main
module Main (
  input  [7:0] in_1,
  input  in_2,
  input  in_3,
  input  [3:0] in_4
);

  wire and_1_out, and_3_out, and_4_out, and_6_out, and_7_out, and_8_out, and_9_out, and_10_out, and_11_out,
       button_1_out, button_2_out, button_3_out, button_4_out, button_5_out, button_6_out, button_7_out,
       button_8_out, button_9_out, cdm_8_1_p2, cdm_8_1_p4, cdm_8_1_p5, cdm_8_1_p6, cdm_8_1_p7, cdm_8_1_p8,
       cdm_8_1_p9, cdm_8_1_p10, clk, code, comparator_1_eq, comparator_2_eq, comparator_3_eq, data,
       decoder_1_out0, decoder_1_out1, gsdd_1_draw, gsdd_1_lose, gsdd_1_win, mem, not_1_out, not_2_out,
       rd_wr_prime, rset, y_n, y_n_1;
  wire [0:0] tttc_1_hout, tttc_1_vout, tttc_2_hout, tttc_3_hout, tttc_4_vout, tttc_7_vout;
  wire [1:0] sdr_1_h0, sdr_1_h1, sdr_1_h2, sdr_1_v0, sdr_1_v1, sdr_1_v2;
  wire [3:0] tttc_1_l0, tttc_1_l1, tttc_1_l2, tttc_1_l3, tttc_2_l0, tttc_2_l1, tttc_2_l2, tttc_2_l3,
       tttc_3_l0, tttc_3_l1, tttc_3_l2, tttc_3_l3, tttc_4_l0, tttc_4_l1, tttc_4_l2, tttc_4_l3, tttc_5_l0,
       tttc_5_l1, tttc_5_l2, tttc_5_l3, tttc_6_l0, tttc_6_l1, tttc_6_l2, tttc_6_l3, tttc_7_l0, tttc_7_l1,
       tttc_7_l2, tttc_7_l3, tttc_8_l0, tttc_8_l1, tttc_8_l2, tttc_8_l3, tttc_9_l0, tttc_9_l1, tttc_9_l2,
       tttc_9_l3;
  wire [5:0] bpc_1_ready;
  wire [7:0] adddddr, cdm_8_1_p14, cdm_8_1_p15, cdm_8_1_p16, controlled_buffer_1_out,
       controlled_buffer_6_out, controlled_buffer_7_out, controlled_buffer_9_out, IOdat, register_1_q,
       register_2_q, register_3_q, undriven;

  Button R (.out(rset));
  Clock clock_1 (.out(clk));
  Comparator comparator_1 (.a({8{1'b0}}), .b(adddddr), .eq(comparator_1_eq));  // open: gt, lt
  and and_1 (and_1_out, clk, 1'b1, 1'b1, ~1'b0, ~1'b0);  // AND_Gate
  SDR sdr_1 (
    .XY(IOdat[5:2]), .clock(decoder_1_out0), .symID(IOdat[1:0]), .h0(sdr_1_h0), .h1(sdr_1_h1), .h2(sdr_1_h2),
    .v2(sdr_1_v2), .v1(sdr_1_v1), .v0(sdr_1_v0));
  // Probe on cdm_8_1_p2
  // Probe on cdm_8_1_p4
  // Probe on cdm_8_1_p5
  // Probe on cdm_8_1_p6
  and and_2 (y_n, comparator_1_eq, data);
  Decoder #(.disabled(0)) decoder_1 (.out0(decoder_1_out0), .out1(decoder_1_out1), .sel(rd_wr_prime), .en(and_1_out));
  LED led_1 (.in(gsdd_1_lose));
  GSDD gsdd_1 (.score(IOdat[7:6]), .clock(decoder_1_out0), .lose(gsdd_1_lose), .win(gsdd_1_win), .draw(gsdd_1_draw));
  LED led_2 (.in(gsdd_1_win));
  LED led_3 (.in(gsdd_1_draw));
  // Probe on cdm_8_1_p7
  // Probe on cdm_8_1_p8
  and and_3 (and_3_out, rd_wr_prime, y_n);
  and and_4 (and_4_out, ~rd_wr_prime, y_n);  // AND_Gate
  Comparator comparator_2 (.a(8'h1), .b(adddddr), .eq(comparator_2_eq));  // open: gt, lt
  and and_5 (y_n_1, comparator_2_eq, data);
  DotMatrix #(.inputtype("row"), .matrixcols(4), .matrixrows(4)) dotmatrix_1 (
    .row0(tttc_1_l0), .row1(tttc_1_l1), .row2(tttc_1_l2), .row3(tttc_1_l3));
  TTTC tttc_1 (
    .L0(tttc_1_l0), .L1(tttc_1_l1), .L2(tttc_1_l2), .L3(tttc_1_l3), .hout(tttc_1_hout[0]),
    .vin({sdr_1_v0[0], sdr_1_v0[1]}), .vout(tttc_1_vout[0]), .btn(button_1_out),
    .hin({sdr_1_h0[0], sdr_1_h0[1]}));
  Button button_1 (.out(button_1_out));
  DotMatrix #(.inputtype("row"), .matrixcols(4), .matrixrows(4)) dotmatrix_2 (
    .row0(tttc_2_l0), .row1(tttc_2_l1), .row2(tttc_2_l2), .row3(tttc_2_l3));
  TTTC tttc_2 (
    .L0(tttc_2_l0), .L1(tttc_2_l1), .L2(tttc_2_l2), .L3(tttc_2_l3), .hout(tttc_2_hout[0]),
    .vin({sdr_1_v0[0], sdr_1_v0[1]}), .vout(tttc_1_vout[0]), .btn(button_2_out),
    .hin({sdr_1_h1[0], sdr_1_h1[1]}));
  Button button_2 (.out(button_2_out));
  DotMatrix #(.inputtype("row"), .matrixcols(4), .matrixrows(4)) dotmatrix_3 (
    .row0(tttc_3_l0), .row1(tttc_3_l1), .row2(tttc_3_l2), .row3(tttc_3_l3));
  TTTC tttc_3 (
    .L0(tttc_3_l0), .L1(tttc_3_l1), .L2(tttc_3_l2), .L3(tttc_3_l3), .hout(tttc_3_hout[0]),
    .vin({sdr_1_v0[0], sdr_1_v0[1]}), .vout(tttc_1_vout[0]), .btn(button_3_out),
    .hin({sdr_1_h2[0], sdr_1_h2[1]}));
  Button button_3 (.out(button_3_out));
  // Probe on cdm_8_1_p9
  // CdM_8 cdm_8_1: pin names not known; wires that end beside it: clk, cdm_8_1_p2, rset, cdm_8_1_p4, cdm_8_1_p5, cdm_8_1_p6, cdm_8_1_p7, cdm_8_1_p8, cdm_8_1_p9, cdm_8_1_p10, mem, rd_wr_prime, adddddr, cdm_8_1_p14, cdm_8_1_p15, cdm_8_1_p16, cdm_8_1_p16
  and and_6 (and_6_out, rd_wr_prime, y_n_1);
  and and_7 (and_7_out, ~rd_wr_prime, y_n_1);  // AND_Gate
  // Probe on IOdat
  Decoder #(.disabled(0)) decoder_2 (.out0(code), .out1(data), .sel(cdm_8_1_p10), .en(mem));
  assign controlled_buffer_1_out = not_1_out ? cdm_8_1_p14 : 8'bz;  // Controlled_Buffer controlled_buffer_1
  not not_1 (not_1_out, rd_wr_prime);
  assign cdm_8_1_p15 = rd_wr_prime ? controlled_buffer_1_out : 8'bz;  // Controlled_Buffer controlled_buffer_2
  Register register_1 (.D(controlled_buffer_1_out), .en(and_4_out), .Q(register_1_q), .clk(clk), .clr(rset));
  assign controlled_buffer_1_out = and_3_out ? register_1_q : 8'bz;  // Controlled_Buffer controlled_buffer_3
  // Probe on IOdat
  TTTC tttc_4 (
    .L0(tttc_4_l0), .L1(tttc_4_l1), .L2(tttc_4_l2), .L3(tttc_4_l3), .hout(tttc_1_hout[0]),
    .vin({sdr_1_v1[0], sdr_1_v1[1]}), .vout(tttc_4_vout[0]), .btn(button_4_out),
    .hin({sdr_1_h0[0], sdr_1_h0[1]}));
  DotMatrix #(.inputtype("row"), .matrixcols(4), .matrixrows(4)) dotmatrix_4 (
    .row0(tttc_4_l0), .row1(tttc_4_l1), .row2(tttc_4_l2), .row3(tttc_4_l3));
  Button button_4 (.out(button_4_out));
  DotMatrix #(.inputtype("row"), .matrixcols(4), .matrixrows(4)) dotmatrix_5 (
    .row0(tttc_5_l0), .row1(tttc_5_l1), .row2(tttc_5_l2), .row3(tttc_5_l3));
  TTTC tttc_5 (
    .L0(tttc_5_l0), .L1(tttc_5_l1), .L2(tttc_5_l2), .L3(tttc_5_l3), .hout(tttc_2_hout[0]),
    .vin({sdr_1_v1[0], sdr_1_v1[1]}), .vout(tttc_4_vout[0]), .btn(button_5_out),
    .hin({sdr_1_h1[0], sdr_1_h1[1]}));
  Button button_5 (.out(button_5_out));
  DotMatrix #(.inputtype("row"), .matrixcols(4), .matrixrows(4)) dotmatrix_6 (
    .row0(tttc_6_l0), .row1(tttc_6_l1), .row2(tttc_6_l2), .row3(tttc_6_l3));
  TTTC tttc_6 (
    .L0(tttc_6_l0), .L1(tttc_6_l1), .L2(tttc_6_l2), .L3(tttc_6_l3), .hout(tttc_3_hout[0]),
    .vin({sdr_1_v1[0], sdr_1_v1[1]}), .vout(tttc_4_vout[0]), .btn(button_6_out),
    .hin({sdr_1_h2[0], sdr_1_h2[1]}));
  Button button_6 (.out(button_6_out));
  // Probe on adddddr
  Pull_Resistor pull_resistor_1 (.node(IOdat));
  assign IOdat = and_4_out ? controlled_buffer_1_out : 8'bz;  // Controlled_Buffer controlled_buffer_4
  assign cdm_8_1_p16 = not_2_out ? 8'h80 : 8'bz;  // Controlled_Buffer controlled_buffer_5
  not not_2 (not_2_out, and_4_out);
  Register register_2 (.D(controlled_buffer_6_out), .en(and_7_out), .Q(register_2_q), .clk(clk), .clr(rset));
  and and_8 (and_8_out, ~y_n, data);  // AND_Gate
  assign controlled_buffer_6_out = and_6_out ? register_2_q : 8'bz;  // Controlled_Buffer controlled_buffer_6
  assign controlled_buffer_7_out = and_7_out ? controlled_buffer_6_out : 8'bz;  // Controlled_Buffer controlled_buffer_7
  DotMatrix #(.inputtype("row"), .matrixcols(4), .matrixrows(4)) dotmatrix_7 (
    .row0(tttc_7_l0), .row1(tttc_7_l1), .row2(tttc_7_l2), .row3(tttc_7_l3));
  TTTC tttc_7 (
    .L0(tttc_7_l0), .L1(tttc_7_l1), .L2(tttc_7_l2), .L3(tttc_7_l3), .hout(tttc_1_hout[0]),
    .vin({sdr_1_v2[0], sdr_1_v2[1]}), .vout(tttc_7_vout[0]), .btn(button_7_out),
    .hin({sdr_1_h0[0], sdr_1_h0[1]}));
  Button button_7 (.out(button_7_out));
  DotMatrix #(.inputtype("row"), .matrixcols(4), .matrixrows(4)) dotmatrix_8 (
    .row0(tttc_8_l0), .row1(tttc_8_l1), .row2(tttc_8_l2), .row3(tttc_8_l3));
  TTTC tttc_8 (
    .L0(tttc_8_l0), .L1(tttc_8_l1), .L2(tttc_8_l2), .L3(tttc_8_l3), .hout(tttc_2_hout[0]),
    .vin({sdr_1_v2[0], sdr_1_v2[1]}), .vout(tttc_7_vout[0]), .btn(button_8_out),
    .hin({sdr_1_h1[0], sdr_1_h1[1]}));
  Button button_8 (.out(button_8_out));
  TTTC tttc_9 (
    .L0(tttc_9_l0), .L1(tttc_9_l1), .L2(tttc_9_l2), .L3(tttc_9_l3), .hout(tttc_3_hout[0]),
    .vin({sdr_1_v2[0], sdr_1_v2[1]}), .vout(tttc_7_vout[0]), .btn(button_9_out),
    .hin({sdr_1_h2[0], sdr_1_h2[1]}));
  DotMatrix #(.inputtype("row"), .matrixcols(4), .matrixrows(4)) dotmatrix_9 (
    .row0(tttc_9_l0), .row1(tttc_9_l1), .row2(tttc_9_l2), .row3(tttc_9_l3));
  Button button_9 (.out(button_9_out));
  RAM ram_1 (
    .addr(adddddr), .data(controlled_buffer_1_out), .sel(and_8_out), .clk(clk), .ld(rd_wr_prime));  // open: clr
  ROM rom_1 (.addr(adddddr), .data(controlled_buffer_1_out), .sel(code));
  Pull_Resistor pull_resistor_2 (.node(controlled_buffer_7_out[0]));
  BPC bpc_1 (
    .v2(tttc_7_vout[0]), .v1(tttc_4_vout[0]), .v0(tttc_1_vout[0]), .h0(tttc_1_hout[0]), .h1(tttc_2_hout[0]),
    .h2(tttc_3_hout[0]), .coord(bpc_1_ready[5:2]), .reset(decoder_1_out1), .ready(bpc_1_ready[0]));
  // Probe on controlled_buffer_1_out
  assign IOdat = decoder_1_out1 ? {2'b10, bpc_1_ready[5:2], 1'b0, bpc_1_ready[0]} : 8'bz;  // Controlled_Buffer controlled_buffer_8
  Comparator comparator_3 (.a({8{1'b1}}), .b(adddddr), .eq(comparator_3_eq));  // open: gt, lt
  and and_9 (and_9_out, comparator_3_eq, data);
  and and_10 (and_10_out, rd_wr_prime, and_9_out);
  and and_11 (and_11_out, ~rd_wr_prime, and_9_out);  // AND_Gate
  Register register_3 (.D(undriven), .en(and_11_out), .Q(register_3_q), .clk(clk), .clr(rset));
  assign controlled_buffer_9_out = and_10_out ? register_3_q : 8'bz;  // Controlled_Buffer controlled_buffer_9

  // Other names for the same wires on the sheet: IOsel = clk; READwrite = rd_wr_prime

  // Notes on the sheet:
  //   contents of rom_1 (hex, n*v repeats v):
  //   d4
endmodule

module TTTC (
  input  [1:0] hin,
  input  [1:0] vin,
  input  btn,
  output [3:0] L0,
  output [3:0] L1,
  output [3:0] L2,
  output [3:0] L3,
  output vout,
  output hout
);

  wire and_1_out;
  wire [1:0] register_1_q;

  Transistor #(.\type ("n")) transistor_1 (.in(1'b0), .out(hout), .gate(btn));
  Register #(.width(2)) register_1 (.D({vin[0], hin[0]}), .Q(register_1_q), .clk(and_1_out));  // open: en, clr
  and and_1 (and_1_out, hin[1], vin[1]);
  ROM #(.addrWidth(2), .dataWidth(16)) rom_1 (.addr(register_1_q), .data({L3, L2, L1, L0}));  // open: sel
  // DotMatrix #(.inputtype("row"), .matrixcols(4), .matrixrows(4)) dotmatrix_1: pin names not known; wires that end beside it: L0, L1, L2, L3

  assign vout = hout;

  // Notes on the sheet:
  //   contents of rom_1 (hex, n*v repeats v):
  //   0 6996 9249 6886
endmodule

module SDR (
  input  [3:0] XY,
  input  clock,
  input  [1:0] symID,
  output [1:0] h0,
  output [1:0] h1,
  output [1:0] h2,
  output [1:0] v2,
  output [1:0] v1,
  output [1:0] v0
);

  wire comparator_1_eq, comparator_2_eq, comparator_3_eq, comparator_4_eq, comparator_5_eq, comparator_6_eq;

  Comparator #(.width(2)) comparator_1 (.a(XY[3:2]), .b(2'b00), .eq(comparator_1_eq));  // open: gt, lt
  Comparator #(.width(2)) comparator_2 (.a(XY[3:2]), .b(2'b01), .eq(comparator_2_eq));  // open: gt, lt
  Comparator #(.width(2)) comparator_3 (.a(XY[3:2]), .b(2'b10), .eq(comparator_3_eq));  // open: gt, lt
  Comparator #(.width(2)) comparator_4 (.a(XY[1:0]), .b(2'b00), .eq(comparator_4_eq));  // open: gt, lt
  Comparator #(.width(2)) comparator_5 (.a(XY[1:0]), .b(2'b01), .eq(comparator_5_eq));  // open: gt, lt
  Comparator #(.width(2)) comparator_6 (.a(XY[1:0]), .b(2'b10), .eq(comparator_6_eq));  // open: gt, lt
  Transistor #(.\type ("n")) transistor_1 (.in(clock), .out(v1[0]), .gate(comparator_2_eq));
  Transistor #(.\type ("n")) transistor_2 (.in(clock), .out(v2[0]), .gate(comparator_3_eq));
  Transistor #(.\type ("n")) transistor_3 (.in(clock), .out(v0[0]), .gate(comparator_1_eq));
  Transistor #(.\type ("n")) transistor_4 (.in(clock), .out(h1[0]), .gate(comparator_5_eq));
  Transistor #(.\type ("n")) transistor_5 (.in(clock), .out(h2[0]), .gate(comparator_6_eq));
  Transistor #(.\type ("n")) transistor_6 (.in(clock), .out(h0[0]), .gate(comparator_4_eq));

  assign h0[1] = symID[0];
  assign h1[1] = symID[0];
  assign h2[1] = symID[0];
  assign v0[1] = symID[1];
  assign v1[1] = symID[1];
  assign v2[1] = symID[1];
endmodule

// BPD
module BPC (
  input  v2,
  input  v1,
  input  v0,
  input  h0,
  input  h1,
  input  h2,
  input  reset,
  output [3:0] coord,
  output ready
);

  wire and_1_out, or_1_out, or_2_out;
  wire [1:0] rom_1_data, rom_2_data;
  wire [2:0] not_1_out, not_6_out;

  Pull_Resistor #(.pull(1)) pull_resistor_1 (.node(v2));
  Pull_Resistor #(.pull(1)) pull_resistor_2 (.node(v1));
  Pull_Resistor #(.pull(1)) pull_resistor_3 (.node(v0));
  Pull_Resistor #(.pull(1)) pull_resistor_4 (.node(h0));
  Pull_Resistor #(.pull(1)) pull_resistor_5 (.node(h1));
  Pull_Resistor #(.pull(1)) pull_resistor_6 (.node(h2));
  not not_1 (not_1_out[0], v2);
  not not_2 (not_1_out[1], v1);
  not not_3 (not_1_out[2], v0);
  not not_4 (not_6_out[2], h0);
  not not_5 (not_6_out[1], h1);
  not not_6 (not_6_out[0], h2);
  or or_1 (or_1_out, not_1_out[0], not_1_out[1], not_1_out[2]);
  or or_2 (or_2_out, not_6_out[0], not_6_out[1], not_6_out[2]);
  ROM #(.addrWidth(3), .dataWidth(2)) rom_1 (.addr(not_1_out), .data(rom_1_data));  // open: sel
  and and_1 (and_1_out, or_1_out, or_2_out);
  ROM #(.addrWidth(3), .dataWidth(2)) rom_2 (.addr(not_6_out), .data(rom_2_data));  // open: sel
  Register #(.width(4), .trigger("high")) register_1 (
    .D({rom_1_data, rom_2_data}), .Q(coord), .clk(and_1_out));  // open: en, clr
  S_R_Flip_Flop s_r_ff_1 (.Q(ready), .preset(and_1_out), .reset(reset));  // open: S, clk, R, Qn, en

  // Notes on the sheet:
  //   contents of rom_1 (hex, n*v repeats v):
  //   3 2 1 3 0 3 3 3
  //   contents of rom_2 (hex, n*v repeats v):
  //   3 2 1 3 0 3 3 3
endmodule

// WLD
module GSDD (
  input  [1:0] score,
  input  clock,
  output lose,
  output win,
  output draw
);

  wire undriven;
  wire [1:0] register_1_q;

  Register #(.width(2)) register_1 (.D(score), .en(undriven), .Q(register_1_q), .clk(clock));  // open: clr
  Comparator #(.width(2)) comparator_1 (.a(register_1_q), .b(2'b00), .eq(lose));  // open: gt, lt
  Comparator #(.width(2)) comparator_2 (.a(register_1_q), .b(2'b01), .eq(win));  // open: gt, lt
  Comparator #(.width(2)) comparator_3 (.a(register_1_q), .b(2'b11), .eq(draw));  // open: gt, lt
endmodule
