// Logisim project another_sdr.circ as structural Verilog: 1 circuit, main circuit SDR
module SDR (
  input  [3:0] XY,
  input  [1:0] symID,
  input  clock,
  output [1:0] H0,
  output [1:0] H1,
  output [1:0] H2,
  output [1:0] V0,
  output [1:0] V1,
  output [1:0] V2
);

  wire comparator_1_eq, comparator_2_eq, comparator_3_eq, comparator_4_eq, comparator_5_eq, comparator_6_eq;

  Comparator #(.width(2)) comparator_1 (.a(2'b00), .b(XY[1:0]), .eq(comparator_1_eq));  // open: gt, lt
  Comparator #(.width(2)) comparator_2 (.a(2'b01), .b(XY[1:0]), .eq(comparator_2_eq));  // open: gt, lt
  Comparator #(.width(2)) comparator_3 (.a(2'b10), .b(XY[1:0]), .eq(comparator_3_eq));  // open: gt, lt
  Comparator #(.width(2)) comparator_4 (.a(2'b00), .b(XY[3:2]), .eq(comparator_4_eq));  // open: gt, lt
  Multiplexer #(.enable("false")) multiplexer_1 (.in1(symID[0]), .out(H0[0]), .sel(comparator_1_eq));  // open: in0
  Multiplexer #(.enable("false")) multiplexer_2 (.in1(symID[0]), .out(H1[0]), .sel(comparator_2_eq));  // open: in0
  Multiplexer #(.enable("false")) multiplexer_3 (.in1(symID[0]), .out(H2[0]), .sel(comparator_3_eq));  // open: in0
  Multiplexer #(.enable("false")) multiplexer_4 (.in1(symID[1]), .out(V0[0]), .sel(comparator_4_eq));  // open: in0
  Multiplexer #(.enable("false")) multiplexer_5 (.in1(symID[1]), .out(V1[0]), .sel(comparator_5_eq));  // open: in0
  Comparator #(.width(2)) comparator_5 (.a(2'b01), .b(XY[3:2]), .eq(comparator_5_eq));  // open: gt, lt
  Multiplexer #(.enable("false")) multiplexer_6 (.in1(symID[1]), .out(V2[0]), .sel(comparator_6_eq));  // open: in0
  Comparator #(.width(2)) comparator_6 (.a(2'b10), .b(XY[3:2]), .eq(comparator_6_eq));  // open: gt, lt
  Multiplexer #(.enable("false")) multiplexer_7 (.in1(clock), .out(H0[1]), .sel(comparator_1_eq));  // open: in0
  Multiplexer #(.enable("false")) multiplexer_8 (.in1(clock), .out(H1[1]), .sel(comparator_2_eq));  // open: in0
  Multiplexer #(.enable("false")) multiplexer_9 (.in1(clock), .out(H2[1]), .sel(comparator_3_eq));  // open: in0
  Multiplexer #(.enable("false")) multiplexer_10 (.in1(clock), .out(V0[1]), .sel(comparator_4_eq));  // open: in0
  Multiplexer #(.enable("false")) multiplexer_11 (.in1(clock), .out(V1[1]), .sel(comparator_5_eq));  // open: in0
  Multiplexer #(.enable("false")) multiplexer_12 (.in1(clock), .out(V2[1]), .sel(comparator_6_eq));  // open: in0
endmodule
