// Logisim project another_version.circ as structural Verilog: 5 circuits, main circuit main
module main (
);

  wire [3:0] tic_tac_toe_cell_1_l0, tic_tac_toe_cell_1_l1, tic_tac_toe_cell_1_l2, tic_tac_toe_cell_1_l3,
       tic_tac_toe_cell_2_l0, tic_tac_toe_cell_2_l1, tic_tac_toe_cell_2_l2, tic_tac_toe_cell_2_l3,
       tic_tac_toe_cell_3_l0, tic_tac_toe_cell_3_l1, tic_tac_toe_cell_3_l2, tic_tac_toe_cell_3_l3,
       tic_tac_toe_cell_4_l0, tic_tac_toe_cell_4_l1, tic_tac_toe_cell_4_l2, tic_tac_toe_cell_4_l3,
       tic_tac_toe_cell_5_l0, tic_tac_toe_cell_5_l1, tic_tac_toe_cell_5_l2, tic_tac_toe_cell_5_l3,
       tic_tac_toe_cell_6_l0, tic_tac_toe_cell_6_l1, tic_tac_toe_cell_6_l2, tic_tac_toe_cell_6_l3,
       tic_tac_toe_cell_7_l0, tic_tac_toe_cell_7_l1, tic_tac_toe_cell_7_l2, tic_tac_toe_cell_7_l3,
       tic_tac_toe_cell_8_l0, tic_tac_toe_cell_8_l1, tic_tac_toe_cell_8_l2, tic_tac_toe_cell_8_l3,
       tic_tac_toe_cell_9_l0, tic_tac_toe_cell_9_l1, tic_tac_toe_cell_9_l2, tic_tac_toe_cell_9_l3;

  Tic_Tac_Toe_Cell tic_tac_toe_cell_1 (
    .L0(tic_tac_toe_cell_1_l0), .L1(tic_tac_toe_cell_1_l1), .L2(tic_tac_toe_cell_1_l2),
    .L3(tic_tac_toe_cell_1_l3));  // open: hin, vin, vout, hout, button
  Tic_Tac_Toe_Cell tic_tac_toe_cell_2 (
    .L0(tic_tac_toe_cell_2_l0), .L1(tic_tac_toe_cell_2_l1), .L2(tic_tac_toe_cell_2_l2),
    .L3(tic_tac_toe_cell_2_l3));  // open: hin, vin, vout, hout, button
  Tic_Tac_Toe_Cell tic_tac_toe_cell_3 (
    .L0(tic_tac_toe_cell_3_l0), .L1(tic_tac_toe_cell_3_l1), .L2(tic_tac_toe_cell_3_l2),
    .L3(tic_tac_toe_cell_3_l3));  // open: hin, vin, vout, hout, button
  DotMatrix #(.inputtype("row"), .matrixcols(4), .matrixrows(4)) dotmatrix_1 (
    .row0(tic_tac_toe_cell_1_l0), .row1(tic_tac_toe_cell_1_l1), .row2(tic_tac_toe_cell_1_l2),
    .row3(tic_tac_toe_cell_1_l3));
  Button button_1 ();  // open: out
  DotMatrix #(.inputtype("row"), .matrixcols(4), .matrixrows(4)) dotmatrix_2 (
    .row0(tic_tac_toe_cell_2_l0), .row1(tic_tac_toe_cell_2_l1), .row2(tic_tac_toe_cell_2_l2),
    .row3(tic_tac_toe_cell_2_l3));
  Button button_2 ();  // open: out
  DotMatrix #(.inputtype("row"), .matrixcols(4), .matrixrows(4)) dotmatrix_3 (
    .row0(tic_tac_toe_cell_3_l0), .row1(tic_tac_toe_cell_3_l1), .row2(tic_tac_toe_cell_3_l2),
    .row3(tic_tac_toe_cell_3_l3));
  Button button_3 ();  // open: out
  Tic_Tac_Toe_Cell tic_tac_toe_cell_4 (
    .L0(tic_tac_toe_cell_4_l0), .L1(tic_tac_toe_cell_4_l1), .L2(tic_tac_toe_cell_4_l2),
    .L3(tic_tac_toe_cell_4_l3));  // open: hin, vin, vout, hout, button
  Tic_Tac_Toe_Cell tic_tac_toe_cell_5 (
    .L0(tic_tac_toe_cell_5_l0), .L1(tic_tac_toe_cell_5_l1), .L2(tic_tac_toe_cell_5_l2),
    .L3(tic_tac_toe_cell_5_l3));  // open: hin, vin, vout, hout, button
  Tic_Tac_Toe_Cell tic_tac_toe_cell_6 (
    .L0(tic_tac_toe_cell_6_l0), .L1(tic_tac_toe_cell_6_l1), .L2(tic_tac_toe_cell_6_l2),
    .L3(tic_tac_toe_cell_6_l3));  // open: hin, vin, vout, hout, button
  DotMatrix #(.inputtype("row"), .matrixcols(4), .matrixrows(4)) dotmatrix_4 (
    .row0(tic_tac_toe_cell_4_l0), .row1(tic_tac_toe_cell_4_l1), .row2(tic_tac_toe_cell_4_l2),
    .row3(tic_tac_toe_cell_4_l3));
  Button button_4 ();  // open: out
  DotMatrix #(.inputtype("row"), .matrixcols(4), .matrixrows(4)) dotmatrix_5 (
    .row0(tic_tac_toe_cell_5_l0), .row1(tic_tac_toe_cell_5_l1), .row2(tic_tac_toe_cell_5_l2),
    .row3(tic_tac_toe_cell_5_l3));
  Button button_5 ();  // open: out
  DotMatrix #(.inputtype("row"), .matrixcols(4), .matrixrows(4)) dotmatrix_6 (
    .row0(tic_tac_toe_cell_6_l0), .row1(tic_tac_toe_cell_6_l1), .row2(tic_tac_toe_cell_6_l2),
    .row3(tic_tac_toe_cell_6_l3));
  Button button_6 ();  // open: out
  Tic_Tac_Toe_Cell tic_tac_toe_cell_7 (
    .L0(tic_tac_toe_cell_7_l0), .L1(tic_tac_toe_cell_7_l1), .L2(tic_tac_toe_cell_7_l2),
    .L3(tic_tac_toe_cell_7_l3));  // open: hin, vin, vout, hout, button
  Tic_Tac_Toe_Cell tic_tac_toe_cell_8 (
    .L0(tic_tac_toe_cell_8_l0), .L1(tic_tac_toe_cell_8_l1), .L2(tic_tac_toe_cell_8_l2),
    .L3(tic_tac_toe_cell_8_l3));  // open: hin, vin, vout, hout, button
  Tic_Tac_Toe_Cell tic_tac_toe_cell_9 (
    .L0(tic_tac_toe_cell_9_l0), .L1(tic_tac_toe_cell_9_l1), .L2(tic_tac_toe_cell_9_l2),
    .L3(tic_tac_toe_cell_9_l3));  // open: hin, vin, vout, hout, button
  DotMatrix #(.inputtype("row"), .matrixcols(4), .matrixrows(4)) dotmatrix_7 (
    .row0(tic_tac_toe_cell_7_l0), .row1(tic_tac_toe_cell_7_l1), .row2(tic_tac_toe_cell_7_l2),
    .row3(tic_tac_toe_cell_7_l3));
  Button button_7 ();  // open: out
  DotMatrix #(.inputtype("row"), .matrixcols(4), .matrixrows(4)) dotmatrix_8 (
    .row0(tic_tac_toe_cell_8_l0), .row1(tic_tac_toe_cell_8_l1), .row2(tic_tac_toe_cell_8_l2),
    .row3(tic_tac_toe_cell_8_l3));
  Button button_8 ();  // open: out
  DotMatrix #(.inputtype("row"), .matrixcols(4), .matrixrows(4)) dotmatrix_9 (
    .row0(tic_tac_toe_cell_9_l0), .row1(tic_tac_toe_cell_9_l1), .row2(tic_tac_toe_cell_9_l2),
    .row3(tic_tac_toe_cell_9_l3));
  Button button_9 ();  // open: out
endmodule

// tttc
module Tic_Tac_Toe_Cell (
  input  [1:0] hin,
  input  [1:0] vin,
  input  button,
  output [3:0] L0,
  output [3:0] L1,
  output [3:0] L2,
  output hout,
  output [3:0] L3,
  output vout
);

  wire and_1_out;
  wire [1:0] register_1_q;

  Transistor #(.\type ("n")) transistor_1 (.in(1'b0), .out(hout), .gate(button));
  and and_1 (and_1_out, hin[1], vin[1]);
  Register #(.width(2)) register_1 (.D({vin[0], hin[0]}), .en(1'b1), .Q(register_1_q), .clk(and_1_out));  // open: clr
  ROM #(.addrWidth(2), .dataWidth(16)) rom_1 (.addr(register_1_q), .data({L3, L2, L1, L0}));  // open: sel
  DotMatrix #(.inputtype("row"), .matrixcols(4), .matrixrows(4)) dotmatrix_1 (
    .row0(L0), .row1(L1), .row2(L2), .row3(L3));

  assign vout = hout;

  // Notes on the sheet:
  //   contents of rom_1 (hex, n*v repeats v):
  //   0 6996 9429 f88f
endmodule

module BPC (
  input  V0,
  input  V1,
  input  V2,
  input  H0,
  input  H1,
  input  reset,
  input  H2,
  output [3:0] XY,
  output ready
);

  wire and_1_out, or_1_out, or_2_out;
  wire [1:0] rom_1_data, rom_2_data;
  wire [2:0] not_1_out, not_4_out;

  not not_1 (not_1_out[0], V0);
  Pull_Resistor #(.pull(1)) pull_resistor_1 (.node(V0));
  Pull_Resistor #(.pull(1)) pull_resistor_2 (.node(V1));
  not not_2 (not_1_out[1], V1);
  not not_3 (not_1_out[2], V2);
  Pull_Resistor #(.pull(1)) pull_resistor_3 (.node(V2));
  Pull_Resistor #(.pull(1)) pull_resistor_4 (.node(H0));
  not not_4 (not_4_out[0], H0);
  not not_5 (not_4_out[1], H1);
  Pull_Resistor #(.pull(1)) pull_resistor_5 (.node(H1));
  Pull_Resistor #(.pull(1)) pull_resistor_6 (.node(H2));
  not not_6 (not_4_out[2], H2);
  or or_1 (or_1_out, not_1_out[0], not_1_out[2], not_1_out[1]);
  or or_2 (or_2_out, not_4_out[0], not_4_out[2], not_4_out[1]);
  and and_1 (and_1_out, or_1_out, or_2_out);
  ROM #(.addrWidth(3), .dataWidth(2)) rom_1 (.addr(not_1_out), .data(rom_1_data));  // open: sel
  ROM #(.addrWidth(3), .dataWidth(2)) rom_2 (.addr(not_4_out), .data(rom_2_data));  // open: sel
  Register #(.width(4)) register_1 (.D({rom_2_data, rom_1_data}), .Q(XY), .clk(and_1_out));  // open: en, clr
  S_R_Flip_Flop s_r_ff_1 (.Q(ready), .preset(and_1_out), .reset(reset));  // open: S, clk, R, Qn, en

  // Notes on the sheet:
  //   contents of rom_1 (hex, n*v repeats v):
  //   0 2 1
  //   contents of rom_2 (hex, n*v repeats v):
  //   0 2 1
endmodule

module SDR (
  input  [3:0] XY,
  input  [1:0] symID,
  input  clock,
  output [1:0] H0,
  output [1:0] H1,
  output [1:0] H2,
  output [1:0] V0,
  output [1:0] V1,
  output [1:0] V2
);

  wire comparator_1_eq, comparator_2_eq, comparator_3_eq, comparator_4_eq, comparator_5_eq, comparator_6_eq;

  Comparator #(.width(2)) comparator_1 (.a(2'b00), .b(XY[1:0]), .eq(comparator_1_eq));  // open: gt, lt
  Comparator #(.width(2)) comparator_2 (.a(2'b01), .b(XY[1:0]), .eq(comparator_2_eq));  // open: gt, lt
  Comparator #(.width(2)) comparator_3 (.a(2'b10), .b(XY[1:0]), .eq(comparator_3_eq));  // open: gt, lt
  Comparator #(.width(2)) comparator_4 (.a(2'b00), .b(XY[3:2]), .eq(comparator_4_eq));  // open: gt, lt
  Multiplexer #(.enable("false")) multiplexer_1 (.in1(symID[0]), .out(H0[0]), .sel(comparator_1_eq));  // open: in0
  Multiplexer #(.enable("false")) multiplexer_2 (.in1(symID[0]), .out(H1[0]), .sel(comparator_2_eq));  // open: in0
  Multiplexer #(.enable("false")) multiplexer_3 (.in1(symID[0]), .out(H2[0]), .sel(comparator_3_eq));  // open: in0
  Multiplexer #(.enable("false")) multiplexer_4 (.in1(symID[1]), .out(V0[0]), .sel(comparator_4_eq));  // open: in0
  Multiplexer #(.enable("false")) multiplexer_5 (.in1(symID[1]), .out(V1[0]), .sel(comparator_5_eq));  // open: in0
  Comparator #(.width(2)) comparator_5 (.a(2'b01), .b(XY[3:2]), .eq(comparator_5_eq));  // open: gt, lt
  Multiplexer #(.enable("false")) multiplexer_6 (.in1(symID[1]), .out(V2[0]), .sel(comparator_6_eq));  // open: in0
  Comparator #(.width(2)) comparator_6 (.a(2'b10), .b(XY[3:2]), .eq(comparator_6_eq));  // open: gt, lt
  Multiplexer #(.enable("false")) multiplexer_7 (.in1(clock), .out(H0[1]), .sel(comparator_1_eq));  // open: in0
  Multiplexer #(.enable("false")) multiplexer_8 (.in1(clock), .out(H1[1]), .sel(comparator_2_eq));  // open: in0
  Multiplexer #(.enable("false")) multiplexer_9 (.in1(clock), .out(H2[1]), .sel(comparator_3_eq));  // open: in0
  Multiplexer #(.enable("false")) multiplexer_10 (.in1(clock), .out(V0[1]), .sel(comparator_4_eq));  // open: in0
  Multiplexer #(.enable("false")) multiplexer_11 (.in1(clock), .out(V1[1]), .sel(comparator_5_eq));  // open: in0
  Multiplexer #(.enable("false")) multiplexer_12 (.in1(clock), .out(V2[1]), .sel(comparator_6_eq));  // open: in0
endmodule

module GSDD (
  input  [1:0] score,
  input  clock,
  output win,
  output lose,
  output draw
);

  wire [1:0] register_1_q;

  Register #(.width(2)) register_1 (.D(score), .Q(register_1_q), .clk(clock));  // open: en, clr
  Comparator #(.width(2)) comparator_1 (.a(2'b01), .b(register_1_q), .eq(win));  // open: gt, lt
  Comparator #(.width(2)) comparator_2 (.a(2'b00), .b(register_1_q), .eq(lose));  // open: gt, lt
  Comparator #(.width(2)) comparator_3 (.a(2'b11), .b(register_1_q), .eq(draw));  // open: gt, lt
endmodule
