// Logisim project try.circ as structural Verilog: 5 circuits, main circuit Main
module Main (
);

  wire and_1_out, and_3_out, button_1_out, button_2_out, button_3_out, button_4_out, button_5_out,
       button_6_out, button_7_out, button_8_out, button_9_out, cdm_8_1_p2, cdm_8_1_p4, cdm_8_1_p5,
       cdm_8_1_p6, cdm_8_1_p7, cdm_8_1_p8, cdm_8_1_p9, cdm_8_1_p10, cdm_8_1_p11, clk, decoder_1_out0,
       decoder_1_out1, decoder_2_out0, decoder_2_out1, gsdd_1_draw, gsdd_1_lose, gsdd_1_win, IOsel,
       not_1_out, READwrite, rset;
  wire [0:0] tttc_1_hout, tttc_1_vout, tttc_2_hout, tttc_3_hout, tttc_4_vout, tttc_7_vout;
  wire [1:0] sdr_1_h0, sdr_1_h1, sdr_1_h2, sdr_1_v0, sdr_1_v1, sdr_1_v2;
  wire [3:0] IOaddr, tttc_1_l0, tttc_1_l1, tttc_1_l2, tttc_1_l3, tttc_2_l0, tttc_2_l1, tttc_2_l2, tttc_2_l3,
       tttc_3_l0, tttc_3_l1, tttc_3_l2, tttc_3_l3, tttc_4_l0, tttc_4_l1, tttc_4_l2, tttc_4_l3, tttc_5_l0,
       tttc_5_l1, tttc_5_l2, tttc_5_l3, tttc_6_l0, tttc_6_l1, tttc_6_l2, tttc_6_l3, tttc_7_l0, tttc_7_l1,
       tttc_7_l2, tttc_7_l3, tttc_8_l0, tttc_8_l1, tttc_8_l2, tttc_8_l3, tttc_9_l0, tttc_9_l1, tttc_9_l2,
       tttc_9_l3;
  wire [7:0] bpc_1_ready, cdm_8_1_p14, cdm_8_1_p15, IOdat;
  wire [7:4] cdm_8_1_p13;

  Button R (.out(rset));
  // Probe on cdm_8_1_p2
  and and_1 (and_1_out, IOsel, IOaddr[0], IOaddr[1], ~IOaddr[2], ~IOaddr[3]);  // AND_Gate
  SDR sdr_1 (
    .XY(IOdat[5:2]), .clock(decoder_1_out0), .symID(IOdat[1:0]), .h0(sdr_1_h0), .h1(sdr_1_h1), .h2(sdr_1_h2),
    .v2(sdr_1_v2), .v1(sdr_1_v1), .v0(sdr_1_v0));
  Clock clock_1 (.out(clk));
  // Probe on cdm_8_1_p6
  // Probe on cdm_8_1_p5
  // Probe on cdm_8_1_p4
  // Probe on cdm_8_1_p7
  Decoder #(.disabled(0)) decoder_1 (.out0(decoder_1_out0), .out1(decoder_1_out1), .sel(READwrite), .en(and_1_out));
  LED led_1 (.in(gsdd_1_lose));
  GSDD gsdd_1 (.score(IOdat[7:6]), .clock(decoder_1_out0), .lose(gsdd_1_lose), .win(gsdd_1_win), .draw(gsdd_1_draw));
  LED led_2 (.in(gsdd_1_win));
  LED led_3 (.in(gsdd_1_draw));
  // Probe on cdm_8_1_p8
  // Probe on cdm_8_1_p9
  DotMatrix #(.inputtype("row"), .matrixcols(4), .matrixrows(4)) dotmatrix_1 (
    .row0(tttc_1_l0), .row1(tttc_1_l1), .row2(tttc_1_l2), .row3(tttc_1_l3));
  TTTC tttc_1 (
    .L0(tttc_1_l0), .L1(tttc_1_l1), .L2(tttc_1_l2), .L3(tttc_1_l3), .hout(tttc_1_hout[0]),
    .vin({sdr_1_v0[0], sdr_1_v0[1]}), .vout(tttc_1_vout[0]), .btn(button_1_out),
    .hin({sdr_1_h0[0], sdr_1_h0[1]}));
  Button button_1 (.out(button_1_out));
  DotMatrix #(.inputtype("row"), .matrixcols(4), .matrixrows(4)) dotmatrix_2 (
    .row0(tttc_2_l0), .row1(tttc_2_l1), .row2(tttc_2_l2), .row3(tttc_2_l3));
  TTTC tttc_2 (
    .L0(tttc_2_l0), .L1(tttc_2_l1), .L2(tttc_2_l2), .L3(tttc_2_l3), .hout(tttc_2_hout[0]),
    .vin({sdr_1_v0[0], sdr_1_v0[1]}), .vout(tttc_1_vout[0]), .btn(button_2_out),
    .hin({sdr_1_h1[0], sdr_1_h1[1]}));
  Button button_2 (.out(button_2_out));
  DotMatrix #(.inputtype("row"), .matrixcols(4), .matrixrows(4)) dotmatrix_3 (
    .row0(tttc_3_l0), .row1(tttc_3_l1), .row2(tttc_3_l2), .row3(tttc_3_l3));
  TTTC tttc_3 (
    .L0(tttc_3_l0), .L1(tttc_3_l1), .L2(tttc_3_l2), .L3(tttc_3_l3), .hout(tttc_3_hout[0]),
    .vin({sdr_1_v0[0], sdr_1_v0[1]}), .vout(tttc_1_vout[0]), .btn(button_3_out),
    .hin({sdr_1_h2[0], sdr_1_h2[1]}));
  Button button_3 (.out(button_3_out));
  and and_2 (IOsel, cdm_8_1_p13[4], cdm_8_1_p13[5], cdm_8_1_p13[6], cdm_8_1_p13[7], decoder_2_out1);
  // CdM_8 cdm_8_1: pin names not known; wires that end beside it: clk, cdm_8_1_p2, rset, cdm_8_1_p4, cdm_8_1_p5, cdm_8_1_p6, cdm_8_1_p7, cdm_8_1_p8, cdm_8_1_p9, cdm_8_1_p10, cdm_8_1_p11, READwrite, {cdm_8_1_p13, IOaddr}, cdm_8_1_p14, cdm_8_1_p15
  not not_1 (not_1_out, READwrite);
  assign cdm_8_1_p15 = READwrite ? IOdat : 8'bz;  // Controlled_Buffer controlled_buffer_1
  Decoder #(.disabled(0)) decoder_2 (.out0(decoder_2_out0), .out1(decoder_2_out1), .sel(cdm_8_1_p10), .en(cdm_8_1_p11));
  assign IOdat = not_1_out ? cdm_8_1_p14 : 8'bz;  // Controlled_Buffer controlled_buffer_2
  DotMatrix #(.inputtype("row"), .matrixcols(4), .matrixrows(4)) dotmatrix_4 (
    .row0(tttc_4_l0), .row1(tttc_4_l1), .row2(tttc_4_l2), .row3(tttc_4_l3));
  TTTC tttc_4 (
    .L0(tttc_4_l0), .L1(tttc_4_l1), .L2(tttc_4_l2), .L3(tttc_4_l3), .hout(tttc_1_hout[0]),
    .vin({sdr_1_v1[0], sdr_1_v1[1]}), .vout(tttc_4_vout[0]), .btn(button_4_out),
    .hin({sdr_1_h0[0], sdr_1_h0[1]}));
  Button button_4 (.out(button_4_out));
  DotMatrix #(.inputtype("row"), .matrixcols(4), .matrixrows(4)) dotmatrix_5 (
    .row0(tttc_5_l0), .row1(tttc_5_l1), .row2(tttc_5_l2), .row3(tttc_5_l3));
  TTTC tttc_5 (
    .L0(tttc_5_l0), .L1(tttc_5_l1), .L2(tttc_5_l2), .L3(tttc_5_l3), .hout(tttc_2_hout[0]),
    .vin({sdr_1_v1[0], sdr_1_v1[1]}), .vout(tttc_4_vout[0]), .btn(button_5_out),
    .hin({sdr_1_h1[0], sdr_1_h1[1]}));
  Button button_5 (.out(button_5_out));
  DotMatrix #(.inputtype("row"), .matrixcols(4), .matrixrows(4)) dotmatrix_6 (
    .row0(tttc_6_l0), .row1(tttc_6_l1), .row2(tttc_6_l2), .row3(tttc_6_l3));
  TTTC tttc_6 (
    .L0(tttc_6_l0), .L1(tttc_6_l1), .L2(tttc_6_l2), .L3(tttc_6_l3), .hout(tttc_3_hout[0]),
    .vin({sdr_1_v1[0], sdr_1_v1[1]}), .vout(tttc_4_vout[0]), .btn(button_6_out),
    .hin({sdr_1_h2[0], sdr_1_h2[1]}));
  Button button_6 (.out(button_6_out));
  // Probe on {cdm_8_1_p13, IOaddr}
  and and_3 (and_3_out, decoder_2_out1, ~IOsel);  // AND_Gate
  Pull_Resistor pull_resistor_1 (.node({cdm_8_1_p13, IOaddr}));
  DotMatrix #(.inputtype("row"), .matrixcols(4), .matrixrows(4)) dotmatrix_7 (
    .row0(tttc_7_l0), .row1(tttc_7_l1), .row2(tttc_7_l2), .row3(tttc_7_l3));
  TTTC tttc_7 (
    .L0(tttc_7_l0), .L1(tttc_7_l1), .L2(tttc_7_l2), .L3(tttc_7_l3), .hout(tttc_1_hout[0]),
    .vin({sdr_1_v2[0], sdr_1_v2[1]}), .vout(tttc_7_vout[0]), .btn(button_7_out),
    .hin({sdr_1_h0[0], sdr_1_h0[1]}));
  Button button_7 (.out(button_7_out));
  DotMatrix #(.inputtype("row"), .matrixcols(4), .matrixrows(4)) dotmatrix_8 (
    .row0(tttc_8_l0), .row1(tttc_8_l1), .row2(tttc_8_l2), .row3(tttc_8_l3));
  TTTC tttc_8 (
    .L0(tttc_8_l0), .L1(tttc_8_l1), .L2(tttc_8_l2), .L3(tttc_8_l3), .hout(tttc_2_hout[0]),
    .vin({sdr_1_v2[0], sdr_1_v2[1]}), .vout(tttc_7_vout[0]), .btn(button_8_out),
    .hin({sdr_1_h1[0], sdr_1_h1[1]}));
  Button button_8 (.out(button_8_out));
  DotMatrix #(.inputtype("row"), .matrixcols(4), .matrixrows(4)) dotmatrix_9 (
    .row0(tttc_9_l0), .row1(tttc_9_l1), .row2(tttc_9_l2), .row3(tttc_9_l3));
  TTTC tttc_9 (
    .L0(tttc_9_l0), .L1(tttc_9_l1), .L2(tttc_9_l2), .L3(tttc_9_l3), .hout(tttc_3_hout[0]),
    .vin({sdr_1_v2[0], sdr_1_v2[1]}), .vout(tttc_7_vout[0]), .btn(button_9_out),
    .hin({sdr_1_h2[0], sdr_1_h2[1]}));
  Button button_9 (.out(button_9_out));
  // Probe on IOdat
  RAM ram_1 (.addr({cdm_8_1_p13, IOaddr}), .data(IOdat), .sel(and_3_out), .clk(clk), .ld(READwrite));  // open: clr
  ROM rom_1 (.addr({cdm_8_1_p13, IOaddr}), .data(IOdat), .sel(decoder_2_out0));
  Pull_Resistor pull_resistor_2 (.node(IOdat));
  BPC bpc_1 (
    .v2(tttc_7_vout[0]), .v1(tttc_4_vout[0]), .v0(tttc_1_vout[0]), .h0(tttc_1_hout[0]), .h1(tttc_2_hout[0]),
    .h2(tttc_3_hout[0]), .coord(bpc_1_ready[3:0]), .ready(bpc_1_ready[7]), .reset(decoder_1_out1));
  assign IOdat = decoder_1_out1 ? {bpc_1_ready[7], 3'b000, bpc_1_ready[3:0]} : 8'bz;  // Controlled_Buffer controlled_buffer_3

  // Notes on the sheet:
  //   contents of rom_1 (hex, n*v repeats v):
  //   d0 f3 d1 80 a1 ee 99 a9 d0 2 74 e1 14 d0 10 b0 8c d3 10 ac 96 96 c2 c1 d0 0 d1 8 d3 0 71 ea 49 d1 ca
  //   11 11 11 c0 d0 3 14 71 ed 3d f6 ba 8a a eb 3a 8f a ed 3a 8f 8f 8f 8d ee 2a c4 d2 e2 12 ab d3 0 8c d1
  //   8 ee 1e d0 10 b0 d1 5 71 e1 57 d3 c0 d0 f3 ee 83 d0 0 d2 8 d1 e2 72 ea 7f b6 d3 3 7b e1 6e d0 f3 d3
  //   40 ee 83 ee 79 d3 c 7b e1 79 d0 f3 d3 0 ee 83 8c 8d d2 8 ee 5d d3 80 d0 f3 c5 c6 16 1e a2 d2 80 7e
  //   e0 8f ee c9 89 5 e1 97 ee c7 ee 99 ee b9 cc 80 d0 3 d1 1 a1 d0 7 a1 d0 f3 0 ea c9 b1 d2 80 36 a e4
  //   c7 bb f e0 b5 ee a8 d1 2 ee 7 d2 0 b9 5 ed c3 8e b9 ee bc d1 1 ee 7 ee a5 d4 0 1 2 4 5 6 8 9 a 0 4 8
  //   1 5 9 2 6 a 0 5 a 8 5 2
endmodule

module TTTC (
  input  [1:0] hin,
  input  [1:0] vin,
  input  btn,
  output [3:0] L0,
  output [3:0] L1,
  output [3:0] L2,
  output [3:0] L3,
  output vout,
  output hout
);

  wire and_1_out, clock_1_out;
  wire [1:0] register_1_q;

  Pull_Resistor pull_resistor_1 (.node(hin[1]));
  Pull_Resistor pull_resistor_2 (.node(vin[1]));
  Transistor #(.\type ("n")) transistor_1 (.in(1'b0), .out(hout), .gate(btn));
  and and_1 (and_1_out, hin[1], vin[1]);
  Clock clock_1 (.out(clock_1_out));
  Register #(.width(2)) register_1 (
    .D({vin[0], hin[0]}), .en(and_1_out), .Q(register_1_q), .clk(clock_1_out));  // open: clr
  ROM #(.addrWidth(2), .dataWidth(16)) rom_1 (.addr(register_1_q), .data({L3, L2, L1, L0}));  // open: sel
  // DotMatrix #(.inputtype("row"), .matrixcols(4), .matrixrows(4)) dotmatrix_1: pin names not known; wires that end beside it: L0, L1, L2, L3

  assign vout = hout;

  // Notes on the sheet:
  //   contents of rom_1 (hex, n*v repeats v):
  //   0 6996 9249 6886
endmodule

module SDR (
  input  [3:0] XY,
  input  clock,
  input  [1:0] symID,
  output [1:0] h0,
  output [1:0] h1,
  output [1:0] h2,
  output [1:0] v2,
  output [1:0] v1,
  output [1:0] v0
);

  wire comparator_1_eq, comparator_2_eq, comparator_3_eq, comparator_4_eq, comparator_5_eq, comparator_6_eq;

  Comparator #(.width(2)) comparator_1 (.a(XY[3:2]), .b(2'b00), .eq(comparator_1_eq));  // open: gt, lt
  Comparator #(.width(2)) comparator_2 (.a(XY[3:2]), .b(2'b01), .eq(comparator_2_eq));  // open: gt, lt
  Comparator #(.width(2)) comparator_3 (.a(XY[3:2]), .b(2'b10), .eq(comparator_3_eq));  // open: gt, lt
  Comparator #(.width(2)) comparator_4 (.a(XY[1:0]), .b(2'b00), .eq(comparator_4_eq));  // open: gt, lt
  Comparator #(.width(2)) comparator_5 (.a(XY[1:0]), .b(2'b01), .eq(comparator_5_eq));  // open: gt, lt
  Comparator #(.width(2)) comparator_6 (.a(XY[1:0]), .b(2'b10), .eq(comparator_6_eq));  // open: gt, lt
  Transistor #(.\type ("n")) transistor_1 (.in(clock), .out(v1[0]), .gate(comparator_2_eq));
  Transistor #(.\type ("n")) transistor_2 (.in(clock), .out(v2[0]), .gate(comparator_3_eq));
  Transistor #(.\type ("n")) transistor_3 (.in(clock), .out(v0[0]), .gate(comparator_1_eq));
  Transistor #(.\type ("n")) transistor_4 (.in(clock), .out(h1[0]), .gate(comparator_5_eq));
  Transistor #(.\type ("n")) transistor_5 (.in(clock), .out(h2[0]), .gate(comparator_6_eq));
  Transistor #(.\type ("n")) transistor_6 (.in(clock), .out(h0[0]), .gate(comparator_4_eq));

  assign h0[1] = symID[0];
  assign h1[1] = symID[0];
  assign h2[1] = symID[0];
  assign v0[1] = symID[1];
  assign v1[1] = symID[1];
  assign v2[1] = symID[1];
endmodule

module BPC (
  input  v2,
  input  v1,
  input  v0,
  input  h0,
  input  h1,
  input  h2,
  input  reset,
  output [3:0] coord,
  output ready
);

  wire and_1_out, and_2_out, clock_1_out, d_ff_1_q, or_1_out, or_2_out;
  wire [1:0] rom_1_data, rom_2_data;
  wire [2:0] not_1_out, not_6_out;

  Pull_Resistor #(.pull(1)) pull_resistor_1 (.node(v2));
  Pull_Resistor #(.pull(1)) pull_resistor_2 (.node(v1));
  Pull_Resistor #(.pull(1)) pull_resistor_3 (.node(v0));
  Pull_Resistor #(.pull(1)) pull_resistor_4 (.node(h0));
  Pull_Resistor #(.pull(1)) pull_resistor_5 (.node(h1));
  Pull_Resistor #(.pull(1)) pull_resistor_6 (.node(h2));
  not not_1 (not_1_out[0], v2);
  not not_2 (not_1_out[1], v1);
  not not_3 (not_1_out[2], v0);
  not not_4 (not_6_out[2], h0);
  not not_5 (not_6_out[1], h1);
  not not_6 (not_6_out[0], h2);
  or or_1 (or_1_out, not_1_out[0], not_1_out[1], not_1_out[2]);
  or or_2 (or_2_out, not_6_out[0], not_6_out[1], not_6_out[2]);
  Clock clock_1 (.out(clock_1_out));
  ROM #(.addrWidth(3), .dataWidth(2)) rom_1 (.addr(not_1_out), .data(rom_1_data));  // open: sel
  and and_1 (and_1_out, or_1_out, or_2_out);
  ROM #(.addrWidth(3), .dataWidth(2)) rom_2 (.addr(not_6_out), .data(rom_2_data));  // open: sel
  Register #(.width(4), .trigger("high")) register_1 (
    .D({rom_1_data, rom_2_data}), .Q(coord), .clk(and_1_out));  // open: en, clr
  S_R_Flip_Flop s_r_ff_1 (.Q(ready), .preset(and_1_out), .reset(and_2_out));  // open: S, clk, R, Qn, en
  and and_2 (and_2_out, d_ff_1_q, ~reset);  // AND_Gate
  D_Flip_Flop #(.trigger("high")) d_ff_1 (.clk(clock_1_out), .D(reset), .Q(d_ff_1_q));  // open: Qn, preset, en, reset

  // Notes on the sheet:
  //   contents of rom_1 (hex, n*v repeats v):
  //   3 2 1 3 0 3 3 3
  //   contents of rom_2 (hex, n*v repeats v):
  //   3 2 1 3 0 3 3 3
endmodule

module GSDD (
  input  [1:0] score,
  input  clock,
  output lose,
  output win,
  output draw
);

  wire clock_1_out;
  wire [1:0] register_1_q;

  Clock clock_1 (.out(clock_1_out));
  Pull_Resistor pull_resistor_1 (.node(clock));
  Register #(.width(2)) register_1 (.D(score), .en(clock), .Q(register_1_q), .clk(clock_1_out));  // open: clr
  Comparator #(.width(2)) comparator_1 (.a(register_1_q), .b(2'b00), .eq(lose));  // open: gt, lt
  Comparator #(.width(2)) comparator_2 (.a(register_1_q), .b(2'b01), .eq(win));  // open: gt, lt
  Comparator #(.width(2)) comparator_3 (.a(register_1_q), .b(2'b11), .eq(draw));  // open: gt, lt
endmodule
